// Logisim project master.circ as structural Verilog: 7 circuits, main circuit main
module main (
);

  wire alu_1_fc, alu_1_fo, alu_1_fs, alu_1_fz, clock_1_out, clock_2_out, clock_3_out, clock_4_out,
       clock_5_out, clock_6_out, clock_7_out, control_1_oregwe, io_1_ogpu_clear, io_1_okeyread,
       keyboard_1_avail, memory_controller_1_gpu_we, regfile_1_oint, regfile_1_oiobusy;
  wire [1:0] control_1_oioop;
  wire [2:0] control_1_oioaddr, control_1_omemop, regfile_1_ointid;
  wire [3:0] control_1_oaluop, control_1_oregid;
  wire [6:0] keyboard_1_data, memory_controller_1_gpu_data;
  wire [15:0] alu_1_busout, control_1_oiobus, control_1_oregbus, io_1_oled, memory_controller_1_databusout;
  wire [15:7] memory_controller_1_gpu_data_2;

  Clock clock_1 (.out(clock_1_out));
  TTY tty_1 (
    .data(memory_controller_1_gpu_data), .clk(clock_1_out), .we(memory_controller_1_gpu_we),
    .clr(io_1_ogpu_clear));
  Clock clock_2 (.out(clock_2_out));
  memory_controller memory_controller_1 (
    .MODE(control_1_omemop), .DataBUSin(memory_controller_1_databusout), .CLK(clock_2_out),
    .GPU_DATA({memory_controller_1_gpu_data_2, memory_controller_1_gpu_data}),
    .GPU_WE(memory_controller_1_gpu_we), .DataBUSout(memory_controller_1_databusout));  // open: GPU_ADDR
  Clock clock_3 (.out(clock_3_out));
  Clock clock_4 (.out(clock_4_out));
  alu alu_1 (
    .op(control_1_oaluop), .busin(alu_1_busout), .clk(clock_4_out), .busout(alu_1_busout), .FC(alu_1_fc),
    .FS(alu_1_fs), .FZ(alu_1_fz), .FO(alu_1_fo));
  control control_1 (
    .in_13(control_1_oiobus), .ialubus(alu_1_busout), .ifs(alu_1_fs), .ifo(alu_1_fo), .ifc(alu_1_fc),
    .ifz(alu_1_fz), .imembus(memory_controller_1_databusout), .iregbus(control_1_oregbus),
    .iint(regfile_1_oint), .iintid(regfile_1_ointid), .ibusy(regfile_1_oiobusy), .iiobus(control_1_oiobus),
    .CLK(clock_3_out), .oregwe(control_1_oregwe), .omemop(control_1_omemop), .oioaddr(control_1_oioaddr),
    .oaluop(control_1_oaluop), .oalubus(alu_1_busout), .omembus(memory_controller_1_databusout),
    .oregbus(control_1_oregbus), .oregid(control_1_oregid), .oiobus(control_1_oiobus), .oioop(control_1_oioop));
  IO io_1 (
    .ikeychar(keyboard_1_data), .ikeyaval(keyboard_1_avail), .CLK(clock_7_out), .iioid(control_1_oioaddr),
    .iiocmd(control_1_oioop), .iiobus(control_1_oiobus), .ogpu_clear(io_1_ogpu_clear),
    .okeyread(io_1_okeyread), .oled(io_1_oled), .oiobus(control_1_oiobus));  // open: obusyassert, ointasssert
  Clock clock_5 (.out(clock_5_out));
  Keyboard keyboard_1 (
    .clk(clock_5_out), .re(io_1_okeyread), .clr(1'b0), .avail(keyboard_1_avail), .data(keyboard_1_data));
  Clock clock_6 (.out(clock_6_out));
  regfile regfile_1 (
    .ibus(control_1_oregbus), .iwe(control_1_oregwe), .iclk(clock_6_out), .irid(control_1_oregid),
    .obus(control_1_oregbus), .oint(regfile_1_oint), .ointid(regfile_1_ointid), .oiobusy(regfile_1_oiobusy));
  Clock clock_7 (.out(clock_7_out));
  // LedBar #(.inputtype("row"), .matrixcols(16)) ledbar_1: pin names not known; wires that end beside it: io_1_oled
endmodule

module memory_controller (
  input  [15:0] DataBUSin,
  input  [2:0] MODE,
  input  CLK,
  output [14:0] GPU_ADDR,
  output [15:0] GPU_DATA,
  output GPU_WE,
  output [15:0] DataBUSout
);

  wire and_3_out, not_1_out, output_enable, write_enable;
  wire [15:0] adder_1_out, general_purpose_memory_dout, multiplexer_1_out, multiplexer_2_out, rom_1_data;
  wire [15:15] RegAddr_q;

  not not_1 (not_1_out, output_enable);
  assign GPU_DATA = not_1_out ? DataBUSin : 16'bz;  // Controlled_Buffer controlled_buffer_1
  and and_1 (write_enable, MODE[2], ~MODE[1], ~MODE[0]);  // AND_Gate
  and and_2 (output_enable, MODE[2], MODE[0]);
  Multiplexer #(.width(16)) multiplexer_1 (.in0(GPU_DATA), .in1(adder_1_out), .out(multiplexer_1_out), .sel(MODE[0]));
  Register #(.width(16)) RegAddr (
    .D(multiplexer_1_out), .en(MODE[1]), .clk(CLK), .Q({RegAddr_q[15], GPU_ADDR}));  // open: clr
  Adder #(.width(16)) adder_1 (.a({RegAddr_q[15], GPU_ADDR}), .b(16'h1), .out(adder_1_out));  // open: cin, cout
  and and_3 (and_3_out, RegAddr_q[15], write_enable);
  ROM #(.addrWidth(16), .dataWidth(16)) rom_1 (.addr({RegAddr_q[15], GPU_ADDR}), .data(rom_1_data));
  RAM #(.addrWidth(16), .asyncread("true"), .dataWidth(16)) general_purpose_memory (
    .addr({RegAddr_q[15], GPU_ADDR}), .we(and_3_out), .oe(1'b1), .clk(CLK), .din(GPU_DATA),
    .dout(general_purpose_memory_dout));
  and and_4 (GPU_WE, ~RegAddr_q[15], write_enable);  // AND_Gate
  Multiplexer #(.width(16)) multiplexer_2 (
    .in0(rom_1_data), .in1(general_purpose_memory_dout), .out(multiplexer_2_out), .sel(RegAddr_q[15]));
  assign DataBUSout = output_enable ? multiplexer_2_out : 16'bz;  // Controlled_Buffer controlled_buffer_2

  // Other names for the same wires on the sheet: Data_in[15:0] = GPU_DATA

  // Notes on the sheet:
  //   15 bit
  //   contents of rom_1 (hex, n*v repeats v):
  //   6180 3980 0 4900 0 3980 3a 4900 d 9880 0 4800 0 7a00 1 4800 0 6f 9880 0 1880 20 9880 0 1880 57 9880
  //   0 1880 6f 9880 0 1880 72 9880 0 1880 6c 9880 0 1880 64 9880 0 1880 0 9880 0 4800 30 6 5056 8003 11*1
  //   2802 7202 5043 13*1 2802 7202 5043 13*1 2802 7202 14*1 2802 7202 14*1 2802 7202 2 5002 2c42 5183
  //   10*1 2802 7202 2 5002 2c42 4003 10*1 2802 7202 6 5076 208e 4802 2802 3002 5103 7*1 2802 7202 2006 76
  //   508b 11*1 2802 7202 6 5076 208e 4c43 10*1 2802 7202 2006 76 8a 5183 10*1 2802 7202 14*1 2802 7202
  //   14*1 32457*0 beef 55*0 dead
  //   VRAM
  //   ROM
  //   RAM
endmodule

module alu (
  input  clk,
  input  [15:0] busin,
  input  [3:0] op,
  output [15:0] busout,
  output FC,
  output FS,
  output FZ,
  output FO
);

  wire adder_1_cout, and_1_out, and_2_out, comparator_1_eq, comparator_2_eq, out_enable, subtractor_1_bout,
       xnor_1_out, xor_1_out;
  wire [14:0] aluout;
  wire [15:0] A, adder_1_out, and_4_out, B, not_2_out, or_1_out, shifter_1_out, shifter_2_out,
       subtractor_1_out, xor_2_out;

  Comparator #(.width(3)) comparator_1 (.a(op[2:0]), .b(3'b000), .eq(comparator_1_eq));  // open: gt, lt
  Comparator #(.width(3)) comparator_2 (.a(op[2:0]), .b(3'b001), .eq(comparator_2_eq));  // open: gt, lt
  not not_1 (out_enable, op[3]);
  and and_1 (and_1_out, op[3], comparator_1_eq);
  and and_2 (and_2_out, op[3], comparator_2_eq);
  Register #(.width(16)) register_1 (.D(busin), .en(and_1_out), .clk(clk), .Q(A), .clr(1'b0));
  Register #(.width(16)) register_2 (.D(busin), .en(and_2_out), .clk(clk), .Q(B), .clr(1'b0));
  assign busout = out_enable ? {FS, aluout} : 16'bz;  // Controlled_Buffer controlled_buffer_1
  Comparator #(.width(16)) comparator_3 (.a({FS, aluout}), .b({16{1'b0}}), .eq(FZ));  // open: gt, lt
  xnor xnor_1 (xnor_1_out, FS, B[15]);
  xor xor_1 (xor_1_out, A[15], B[15]);
  and and_3 (FO, xnor_1_out, xor_1_out);
  Adder #(.width(16)) adder_1 (.a(A), .b(B), .out(adder_1_out), .cin(1'b0), .cout(adder_1_cout));
  Subtractor #(.width(16)) subtractor_1 (.a(A), .b(B), .out(subtractor_1_out), .bin(1'b0), .bout(subtractor_1_bout));
  assign and_4_out = A & B;  // AND_Gate and_4, 16 bits wide
  assign or_1_out = A | B;  // OR_Gate or_1, 16 bits wide
  assign xor_2_out = A ^ B;  // XOR_Gate xor_2, 16 bits wide
  assign not_2_out = ~A;  // NOT_Gate not_2, 16 bits wide
  Shifter #(.width(16)) shifter_1 (.in(A), .\dist (B[3:0]), .out(shifter_1_out));
  Shifter #(.shift("lr"), .width(16)) shifter_2 (.in(A), .\dist (B[3:0]), .out(shifter_2_out));
  Multiplexer #(.select(3)) multiplexer_1 (
    .in0(adder_1_cout), .in1(subtractor_1_bout), .in2(1'b0), .in3(1'b0), .in4(1'b0), .in5(1'b0), .in6(1'b0),
    .in7(1'b0), .out(FC), .sel(op[2:0]));
  Multiplexer #(.select(3), .width(16)) multiplexer_2 (
    .in0(adder_1_out), .in1(subtractor_1_out), .in2(and_4_out), .in3(or_1_out), .in4(xor_2_out),
    .in5(not_2_out), .in6(shifter_1_out), .in7(shifter_2_out), .out({FS, aluout}), .sel(op[2:0]));

  // Other names for the same wires on the sheet: aluout[15] = FS; bin[15:0] = busin; cout = FC; aluop[2:0] = op[2:0];
  //   regid[2:0] = op[2:0]; regwe = op[3]
endmodule

module control (
  input  CLK,
  input  [15:0] ialubus,
  input  ifs,
  input  ifo,
  input  ifc,
  input  ifz,
  input  [15:0] imembus,
  input  [15:0] iregbus,
  input  iint,
  input  [2:0] iintid,
  input  ibusy,
  input  [15:0] iiobus,
  input  [15:0] in_13,
  output [3:0] oaluop,
  output [15:0] oalubus,
  output [2:0] omemop,
  output [15:0] omembus,
  output oregwe,
  output [15:0] oregbus,
  output [3:0] oregid,
  output [1:0] oioop,
  output [15:0] oiobus,
  output [2:0] oioaddr
);

  wire and_1_out, and_2_out, and_3_out, and_4_out, and_5_out, and_6_out, c, flwe, instr_load, isimm, isjump,
       isret, isstack, next_instr, not_1_out, not_2_out, not_3_out, not_4_out, not_5_out, not_6_out, o,
       or_1_out, or_2_out, regds, regsrc, s, should_jump, tempregwe, valid, xnor_1_out, xnor_2_out,
       xor_1_out, xor_2_out, z;
  wire [1:0] alumode, alusrc, memsrc;
  wire [3:0] adder_2_out, cycle, multiplexer_3_out, multiplexer_6_out, opcode;
  wire [7:0] instruction_q;
  wire [15:0] alubus, alubuswrite, iobuswrite, ip, ipnext, membus, membuswrite, multiplexer_1_out,
       multiplexer_2_out, multiplexer_7_out, multiplexer_12_out, regbuswrite, srctempbus, tempreg;
  wire [23:22] rom_1_data;

  not not_1 (not_1_out, oaluop[3]);
  assign alubus = not_1_out ? ialubus : 16'bz;  // Controlled_Buffer controlled_buffer_1
  assign membus = and_5_out ? imembus : 16'bz;  // Controlled_Buffer controlled_buffer_2
  Adder #(.width(16)) adder_1 (.a(ip), .b(16'h1), .out(ipnext), .cin(isimm));  // open: cout
  Multiplexer #(.width(16)) multiplexer_1 (.in0(ipnext), .in1(iobuswrite), .out(multiplexer_1_out), .sel(and_1_out));
  and and_1 (and_1_out, isjump, should_jump);
  Register #(.width(16)) instruction (
    .D(membus), .en(instr_load), .clk(CLK), .Q({opcode, isimm, oioaddr, instruction_q}), .clr(1'b0));
  Register #(.width(16)) u_IP (.D(multiplexer_2_out), .en(next_instr), .clk(CLK), .Q(ip), .clr(1'b0));
  Multiplexer #(.width(16)) multiplexer_2 (.in0(multiplexer_1_out), .in1(membus), .out(multiplexer_2_out), .sel(isret));
  xnor xnor_1 (xnor_1_out, s, o);
  xor xor_1 (xor_1_out, s, o);
  xnor xnor_2 (xnor_2_out, s, o);
  xor xor_2 (xor_2_out, s, o);
  Clock clock_1 ();  // open: out
  and and_2 (and_2_out, oioop[0], oioop[1]);
  Pull_Resistor pull_resistor_1 (.node({opcode, isimm, oioaddr, instruction_q}));
  not not_2 (not_2_out, z);
  or or_1 (or_1_out, z, xor_1_out);
  and and_3 (and_3_out, ~z, xnor_2_out);  // AND_Gate
  not not_3 (not_3_out, s);
  not not_4 (not_4_out, c);
  or or_2 (or_2_out, c, z);
  and and_4 (and_4_out, ~c, ~z);  // AND_Gate
  not not_5 (not_5_out, o);
  assign oalubus = oaluop[3] ? alubuswrite : 16'bz;  // Controlled_Buffer controlled_buffer_3
  and and_5 (and_5_out, omemop[0], omemop[2]);
  not not_6 (not_6_out, and_5_out);
  assign omembus = not_6_out ? membuswrite : 16'bz;  // Controlled_Buffer controlled_buffer_4
  assign oregbus = oregwe ? regbuswrite : 16'bz;  // Controlled_Buffer controlled_buffer_5
  assign oiobus = and_2_out ? iobuswrite : 16'bz;  // Controlled_Buffer controlled_buffer_6
  Multiplexer #(.width(4)) multiplexer_3 (
    .in0(instruction_q[7:4]), .in1(instruction_q[3:0]), .out(multiplexer_3_out), .sel(regds));
  Multiplexer #(.select(4)) multiplexer_4 (
    .in0(1'b1), .in1(z), .in2(not_2_out), .in3(xnor_1_out), .in4(or_1_out), .in5(and_3_out), .in6(xor_2_out),
    .in7(o), .in8(ibusy), .in9(s), .in10(not_3_out), .in11(not_4_out), .in12(or_2_out), .in13(and_4_out),
    .in14(c), .in15(not_5_out), .out(should_jump), .sel({opcode[0], oioaddr}));
  Multiplexer #(.width(4)) multiplexer_5 (.in0(multiplexer_3_out), .in1(4'b0010), .out(oregid), .sel(isstack));
  Adder #(.width(4)) adder_2 (.a(cycle), .b(4'b0001), .out(adder_2_out));  // open: cin, cout
  Register #(.width(4)) u_cycle (.D(multiplexer_6_out), .en(1'b1), .clk(CLK), .Q(cycle), .clr(1'b0));
  Multiplexer #(.width(4)) multiplexer_6 (.in0(adder_2_out), .in1(4'b0000), .out(multiplexer_6_out), .sel(next_instr));
  Register #(.width(4)) flags (.D({ifz, ifc, ifo, ifs}), .en(flwe), .clk(CLK), .Q({z, c, o, s}), .clr(1'b0));
  Register #(.width(16)) u_tempreg (.D(membus), .en(tempregwe), .clk(CLK), .Q(tempreg), .clr(1'b0));
  ROM #(.dataWidth(24)) rom_1 (
    .addr({opcode, cycle}),
    .data({rom_1_data, oioop, isret, isstack, tempregwe, isjump, flwe, omemop, memsrc, instr_load, regsrc, oregwe, regds, alusrc, alumode, valid, next_instr}));
  Pull_Resistor pull_resistor_2 (.node(cycle));
  Pull_Resistor pull_resistor_3 (.node({rom_1_data, oioop, isret, isstack, tempregwe, isjump, flwe, omemop, memsrc, instr_load, regsrc, oregwe, regds, alusrc, alumode, valid, next_instr}));
  Multiplexer #(.width(16)) multiplexer_7 (.in0(ip), .in1(ipnext), .out(multiplexer_7_out), .sel(isjump));
  Multiplexer #(.width(16)) multiplexer_8 (.in0(iregbus), .in1(membus), .out(iobuswrite), .sel(isimm));
  Multiplexer #(.width(16)) multiplexer_9 (.in0(iregbus), .in1(tempreg), .out(srctempbus), .sel(isimm));
  Multiplexer #(.select(2), .width(4)) multiplexer_10 (
    .in0({1'b0, oioaddr}), .in1({3'b100, regds}), .in2(4'b0000), .in3(4'b0001), .out(oaluop), .sel(alumode));
  Multiplexer #(.select(2), .width(16)) multiplexer_11 (
    .in0(iregbus), .in1(iobuswrite), .in2({16{1'b0}}), .in3(16'h1), .out(alubuswrite), .sel(alusrc));
  Multiplexer #(.width(16)) multiplexer_12 (.in0(alubus), .in1(membus), .out(multiplexer_12_out), .sel(regsrc));
  Multiplexer #(.select(2), .width(16)) multiplexer_13 (
    .in0(iregbus), .in1(iobuswrite), .in2(multiplexer_7_out), .in3(srctempbus), .out(membuswrite),
    .sel(memsrc));
  and and_6 (and_6_out, ~oioop[0], oioop[1]);  // AND_Gate
  Multiplexer #(.width(16)) multiplexer_14 (.in0(multiplexer_12_out), .in1(in_13), .out(regbuswrite), .sel(and_6_out));

  // Other names for the same wires on the sheet: fs = ifs; fo = ifo; fc = ifc; fz = ifz; regwe = oregwe;
  //   memop[2:0] = omemop; ioop[1:0] = oioop; funct[2:0] = oioaddr; aluop[3:0] = oaluop; busy = ibusy; int = iint;
  //   intid[2:0] = iintid; iobus[15:0] = iiobus; regbus[15:0] = iregbus; regid[3:0] = oregid;
  //   srcbus[15:0] = iobuswrite

  // Notes on the sheet:
  //   MEM
  //   REG
  //   IO
  //   ALU
  //   REGISTERS
  //   JUMPS
  //   contents of rom_1 (hex, n*v repeats v):
  //   2802 7202 14*1 2802 7202 26 5056 8b 11*1 2802 7202 6 5056 8083 11*1 2802 7202 6 5056 8003 11*1 2802
  //   7202 15043 13*1 2802 7202 15043 13*1 2802 7202 200083 13*1 2802 7202 305043 13*1 2802 7202 25002
  //   2c42 5183 11*1 2802 7202 25002 2c42 4003 11*1 2802 7202 40006 25076 4208e 14802 2802 3002 15103 7*1
  //   2802 7202 42006 76 c508b 11*1 2802 7202 40006 25076 4208e 4c43 10*1 2802 7202 42006 76 4008a 5183
  //   10*1 2802 7202 14*1 2802 7202 14*1
  //   CONTROL SIGNALS
  //   BUSES
endmodule

module regfile (
  input  iclk,
  input  [3:0] irid,
  input  [15:0] ibus,
  input  iwe,
  output [15:0] obus,
  output oint,
  output [2:0] ointid,
  output oiobusy
);

  wire not_1_out, not_2_out;
  wire [15:0] rbus;

  assign rbus = iwe ? ibus : 16'bz;  // Controlled_Buffer controlled_buffer_1
  not not_1 (not_1_out, iwe);
  not not_2 (not_2_out, iwe);
  RAM #(.addrWidth(4), .asyncread("true"), .dataWidth(16), .databus("bidir")) ram_1 (
    .addr(irid), .we(iwe), .oe(not_1_out), .clk(iclk), .data(rbus));
  assign obus = not_2_out ? rbus : 16'bz;  // Controlled_Buffer controlled_buffer_2
  Clock clock_1 ();  // open: out

  assign oint = 1'b0;
  assign ointid = 3'b000;
  assign oiobusy = 1'b0;

  // Other names for the same wires on the sheet: clk = iclk; rid[3:0] = irid; we = iwe
endmodule

module regisiterfile (
  input  CLK,
  input  [15:0] data_in,
  input  wr_enable,
  input  [15:0] IO,
  input  mask_save,
  input  mask_restore,
  input  [3:0] regid,
  output [2:0] INT_ID,
  output INT,
  output BUSY,
  output [15:0] data_out
);

  wire demultiplexer_1_out0, demultiplexer_1_out1, demultiplexer_1_out2, demultiplexer_1_out3,
       demultiplexer_1_out4, demultiplexer_1_out5, demultiplexer_1_out6, demultiplexer_1_out7,
       demultiplexer_1_out8, demultiplexer_1_out9, demultiplexer_1_out10, demultiplexer_1_out11,
       demultiplexer_1_out12, demultiplexer_1_out13, demultiplexer_1_out14, demultiplexer_1_out15, not_1_out,
       or_1_out;
  wire [7:0] and_1_out;
  wire [15:0] mask_saved, multiplexer_1_out, multiplexer_2_out, multiplexer_3_out, r0_out, r1_out, r2_q,
       r3_q, r4_q, r5_q, r6_q, r7_q, r8_q, r9_q, r10_q, r11_q, r12_q, r13_q, r14_q, r15_q;

  Demultiplexer #(.select(4)) demultiplexer_1 (
    .out0(demultiplexer_1_out0), .out1(demultiplexer_1_out1), .out2(demultiplexer_1_out2),
    .out3(demultiplexer_1_out3), .out4(demultiplexer_1_out4), .out5(demultiplexer_1_out5),
    .out6(demultiplexer_1_out6), .out7(demultiplexer_1_out7), .out8(demultiplexer_1_out8),
    .out9(demultiplexer_1_out9), .out10(demultiplexer_1_out10), .out11(demultiplexer_1_out11),
    .out12(demultiplexer_1_out12), .out13(demultiplexer_1_out13), .out14(demultiplexer_1_out14),
    .out15(demultiplexer_1_out15), .in(wr_enable), .sel(regid));
  Register #(.width(16)) mask_storage (.D(r1_out), .en(mask_save), .clk(CLK), .Q(mask_saved));  // open: clr
  Multiplexer #(.width(16)) multiplexer_1 (
    .in0(data_in), .in1(mask_saved), .out(multiplexer_1_out), .sel(mask_restore));
  Multiplexer #(.width(16)) multiplexer_2 (
    .in0(multiplexer_1_out), .in1({16{1'b0}}), .out(multiplexer_2_out), .sel(mask_save));
  or or_1 (or_1_out, demultiplexer_1_out1, mask_save, mask_restore);
  Register #(.width(16)) r0 (.D(IO), .en(1'b1), .clk(CLK), .Q(r0_out));  // open: clr
  Register #(.width(16)) r1 (.D(multiplexer_2_out), .en(or_1_out), .clk(CLK), .Q(r1_out));  // open: clr
  Register #(.width(16)) r2 (.D(data_in), .en(demultiplexer_1_out2), .clk(CLK), .Q(r2_q));  // open: clr
  Register #(.width(16)) r3 (.D(data_in), .en(demultiplexer_1_out3), .clk(CLK), .Q(r3_q));  // open: clr
  Register #(.width(16)) r4 (.D(data_in), .en(demultiplexer_1_out4), .clk(CLK), .Q(r4_q));  // open: clr
  Register #(.width(16)) r5 (.D(data_in), .en(demultiplexer_1_out5), .clk(CLK), .Q(r5_q));  // open: clr
  Register #(.width(16)) r6 (.D(data_in), .en(demultiplexer_1_out6), .clk(CLK), .Q(r6_q));  // open: clr
  Register #(.width(16)) r7 (.D(data_in), .en(demultiplexer_1_out7), .clk(CLK), .Q(r7_q));  // open: clr
  Register #(.width(16)) r8 (.D(data_in), .en(demultiplexer_1_out8), .clk(CLK), .Q(r8_q));  // open: clr
  Register #(.width(16)) r9 (.D(data_in), .en(demultiplexer_1_out9), .clk(CLK), .Q(r9_q));  // open: clr
  Register #(.width(16)) r10 (.D(data_in), .en(demultiplexer_1_out10), .clk(CLK), .Q(r10_q));  // open: clr
  Register #(.width(16)) r11 (.D(data_in), .en(demultiplexer_1_out11), .clk(CLK), .Q(r11_q));  // open: clr
  Register #(.width(16)) r12 (.D(data_in), .en(demultiplexer_1_out12), .clk(CLK), .Q(r12_q));  // open: clr
  Register #(.width(16)) r13 (.D(data_in), .en(demultiplexer_1_out13), .clk(CLK), .Q(r13_q));  // open: clr
  Register #(.width(16)) r14 (.D(data_in), .en(demultiplexer_1_out14), .clk(CLK), .Q(r14_q));  // open: clr
  Register #(.width(16)) r15 (.D(data_in), .en(demultiplexer_1_out15), .clk(CLK), .Q(r15_q));  // open: clr
  assign data_out = not_1_out ? multiplexer_3_out : 16'bz;  // Controlled_Buffer controlled_buffer_1
  Multiplexer #(.select(4), .width(16)) multiplexer_3 (
    .in0(r0_out), .in1(r1_out), .in2(r2_q), .in3(r3_q), .in4(r4_q), .in5(r5_q), .in6(r6_q), .in7(r7_q),
    .in8(r8_q), .in9(r9_q), .in10(r10_q), .in11(r11_q), .in12(r12_q), .in13(r13_q), .in14(r14_q),
    .in15(r15_q), .out(multiplexer_3_out), .sel(regid));
  not not_1 (not_1_out, wr_enable);
  assign and_1_out = r0_out[15:8] & r1_out[15:8];  // AND_Gate and_1, 8 bits wide
  or or_2 (BUSY, r0_out[0], r0_out[1], r0_out[2], r0_out[3], r0_out[4], r0_out[5], r0_out[6], r0_out[7]);
  Priority_Encoder priority_encoder_1 (
    .in0(and_1_out[7]), .in1(and_1_out[6]), .in2(and_1_out[5]), .in3(and_1_out[4]), .in4(and_1_out[3]),
    .in5(and_1_out[2]), .in6(and_1_out[1]), .in7(and_1_out[0]), .out(INT_ID), .gs(INT));  // open: en_in, en_out

  // Other names for the same wires on the sheet: data_tunnel[15:0] = data_in; reg_num[3:0] = regid; we = wr_enable
endmodule

module IO (
  input  CLK,
  input  [15:0] iiobus,
  input  [2:0] iioid,
  input  [1:0] iiocmd,
  input  [6:0] ikeychar,
  input  ikeyaval,
  output [15:0] oiobus,
  output [7:0] ointasssert,
  output [7:0] obusyassert,
  output ogpu_clear,
  output okeyread,
  output [15:0] oled
);

  wire and_2_out, and_3_out, and_4_out, isgpu, iskeyboard, isled, re, we;
  wire [6:0] keyoutput;
  wire [7:0] multiplexer_1_out;
  wire [15:0] multiplexer_2_out;

  or or_1 (okeyread, and_2_out, and_3_out);
  Register register_1 (.D(multiplexer_1_out), .en(okeyread), .clk(CLK), .Q({ointasssert[2], keyoutput}), .clr(1'b0));
  Multiplexer #(.width(8)) multiplexer_1 (
    .in0({8{1'b0}}), .in1({1'b1, ikeychar}), .out(multiplexer_1_out), .sel(ikeyaval));
  and and_1 (ogpu_clear, isgpu, we);
  and and_2 (and_2_out, iskeyboard, re);
  and and_3 (and_3_out, ikeyaval, ~ointasssert[2]);  // AND_Gate
  and and_4 (and_4_out, isled, we);
  and and_5 (we, iiocmd[0], iiocmd[1]);
  and and_6 (re, iiocmd[1], ~iiocmd[0]);  // AND_Gate
  Register #(.width(16)) register_2 (.D(iiobus), .en(and_4_out), .clk(CLK), .Q(oled), .clr(1'b0));
  Multiplexer #(.select(3), .width(16)) multiplexer_2 (
    .in0({16{1'b0}}), .in1({{9{1'b0}}, keyoutput}), .in2({16{1'b0}}), .in3({16{1'b0}}), .in4({16{1'b0}}),
    .in5({16{1'b0}}), .in6({16{1'b0}}), .in7({16{1'b0}}), .out(multiplexer_2_out), .sel(iioid));
  assign oiobus = re ? multiplexer_2_out : 16'bz;  // Controlled_Buffer controlled_buffer_1
  Demultiplexer #(.select(3)) demultiplexer_1 (
    .out1(iskeyboard), .out2(isgpu), .out7(isled), .in(1'b1), .sel(iioid));  // open: out0, out3, out4, out5, out6

  assign obusyassert = {8{1'b0}};
  assign {ointasssert[7:3], ointasssert[1:0]} = {7{1'b0}};

  // Other names for the same wires on the sheet: keychar[6:0] = ikeychar; iobus[15:0] = iiobus; ioid[2:0] = iioid;
  //   keyaval = ikeyaval; keyread = okeyread; key_present = ointasssert[2]

  // Notes on the sheet:
  //   GPU interface
  //   CPU interface
  //   keyboard interface
  //   led interface
  //   currently, only keyboard is meaningfully readable
  //   IO interface
endmodule
